// Logisim project Arch_Project_2.circ as structural Verilog
module main (
  input  [15:0] ALU_input_1,
  input  [2:0] RA,
  input  [15:0] ALU_input_2,
  input  [2:0] RB,
  input  [2:0] RW,
  input  [15:0] ALUresult,
  input  RegWrite,
  input  [15:0] in_8,
  input  [3:0] OP,
  input  [2:0] Funct,
  input  clk,
  output Zero_Flag,
  output [15:0] ALU_output,
  output [15:0] BusA,
  output [15:0] BusB,
  output [15:0] out_16,
  output [1:0] Reg,
  output J,
  output BEQ,
  output Jal,
  output LUI,
  output Jr,
  output MemToReg,
  output ExtOP,
  output RegWrite_2,
  output MemWrite,
  output ALUSrc,
  output MemRead
);

  wire and_1_out, Clock_out, d_ff_1_q, Stall_IF_ID, undriven;
  wire [2:0] alu_control_1_aluctrl;

  IF_ID_Buffer if_id_buffer_1 ();  // open: Fetched_Inst, Incremented_PC, clock, Inc_Pc, Enable, Clear, Imm_17, Op, Cond, Sf, Rs, Rt, Rd, Imm_10
  D_Flip_Flop d_ff_1 (.clk(clk), .D(undriven), .Q(d_ff_1_q));  // open: Qn, preset, en, reset
  and and_1 (and_1_out, clk, d_ff_1_q);
  Inc_PC inc_pc_1 ();  // open: PC, PCToInsMem, IncPC, clk, enable
  Data_Memory data_memory_1 ();  // open: Address, Data_In, Data_Out, MemWrite, MemRead, clk
  Instruction_Memory instruction_memory_1 (.Instruction(out_16));  // open: Address
  // NOR_Gate nor_1 has open pins: in0=Stall_IF_ID, in1=and_1_out, out=open
  Clock Clock (.out(Clock_out));
  // Register_File register_file_1: pin names not known; wires that end beside it: RA, RB, RW, Clock_out, RegWrite, ALUresult, BusA, BusB
  // Control_Unit control_unit_1: pin names not known; wires that end beside it: OP, Funct, Reg, RegWrite_2, ALUSrc, J, BEQ, Jal, LUI, Jr, MemToReg, MemWrite, MemRead, ExtOP
  ALU_Control alu_control_1 (.ALUCtrl(alu_control_1_aluctrl));  // open: OP, Funct
  // ALU alu_1: pin names not known; wires that end beside it: ALU_input_1, ALU_input_2, alu_control_1_aluctrl, Zero_Flag, ALU_output
  Next_PC next_pc_1 ();  // open: Imm, inc_PC, J_JAL_BEQ_NEW_ADD, PCSrc, BusA, Zero_Flag, BEQ, J, JR, JAL
endmodule

module Register_File (
  input  [23:0] BusW,
  input  [2:0] RW,
  input  [2:0] RA,
  input  [2:0] RB,
  input  RegWrite,
  input  Clock,
  output [23:0] BusA,
  output [23:0] BusB
);

  wire and_1_out, and_2_out, and_3_out, and_4_out, and_5_out, and_6_out, and_7_out, and_8_out,
       decoder_1_out0, decoder_1_out1, decoder_1_out2, decoder_1_out3, decoder_1_out4, decoder_1_out5,
       decoder_1_out6, decoder_1_out7;
  wire [23:0] reg_0_q, register_1_q, register_2_q, register_3_q, register_4_q, register_5_q, register_6_q,
       register_7_q;

  Decoder #(.select(3), .enable("false")) decoder_1 (
    .out0(decoder_1_out0), .out1(decoder_1_out1), .out2(decoder_1_out2), .out3(decoder_1_out3),
    .out4(decoder_1_out4), .out5(decoder_1_out5), .out6(decoder_1_out6), .out7(decoder_1_out7), .sel(RW));
  and and_1 (and_1_out, decoder_1_out0, 1'b0);
  and and_2 (and_2_out, decoder_1_out1, RegWrite);
  and and_3 (and_3_out, decoder_1_out2, RegWrite);
  and and_4 (and_4_out, decoder_1_out3, RegWrite);
  and and_5 (and_5_out, decoder_1_out4, RegWrite);
  and and_6 (and_6_out, decoder_1_out5, RegWrite);
  and and_7 (and_7_out, decoder_1_out6, RegWrite);
  and and_8 (and_8_out, decoder_1_out7, RegWrite);
  Register #(.width(24)) reg_0 (.D(BusW), .en(and_1_out), .Q(reg_0_q), .clk(Clock));  // open: clr
  Register #(.width(24)) register_1 (.D(BusW), .en(and_2_out), .Q(register_1_q), .clk(Clock));  // open: clr
  Register #(.width(24)) register_2 (.D(BusW), .en(and_3_out), .Q(register_2_q), .clk(Clock));  // open: clr
  Register #(.width(24)) register_3 (.D(BusW), .en(and_4_out), .Q(register_3_q), .clk(Clock));  // open: clr
  Register #(.width(24)) register_4 (.D(BusW), .en(and_5_out), .Q(register_4_q), .clk(Clock));  // open: clr
  Register #(.width(24)) register_5 (.D(BusW), .en(and_6_out), .Q(register_5_q), .clk(Clock));  // open: clr
  Register #(.width(24)) register_6 (.D(BusW), .en(and_7_out), .Q(register_6_q), .clk(Clock));  // open: clr
  Register #(.width(24)) register_7 (.D(BusW), .en(and_8_out), .Q(register_7_q), .clk(Clock));  // open: clr
  Multiplexer #(.select(3), .width(24), .enable("false")) multiplexer_1 (
    .in0(reg_0_q), .in1(register_1_q), .in2(register_2_q), .in3(register_3_q), .in4(register_4_q),
    .in5(register_5_q), .in6(register_6_q), .in7(register_7_q), .out(BusA), .sel(RA));
  Multiplexer #(.select(3), .width(24), .enable("false")) multiplexer_2 (
    .in0(reg_0_q), .in1(register_1_q), .in2(register_2_q), .in3(register_3_q), .in4(register_4_q),
    .in5(register_5_q), .in6(register_6_q), .in7(register_7_q), .out(BusB), .sel(RB));
endmodule

module Instruction_Memory (
  input  [15:0] Address,
  output [15:0] Instruction
);

  ROM #(.addrWidth(16), .dataWidth(16)) rom_1 (.addr(Address), .data(Instruction));  // open: sel

  // Notes on the sheet:
  //   contents of rom_1 (hex, n*v repeats v):
  //   7a41
endmodule

module ALU (
  input  [23:0] ALU_input_1,
  input  [2:0] ALUCtrl,
  input  [23:0] ALU_input_2,
  output [23:0] ALU_Output,
  output Zero_Flag
);

  wire subtractor_1_bout;
  wire [23:0] adder_1_out, and_2_out, and_3_out, And_out, bit_extender_1_out, bit_extender_2_out, not_1_out,
       or_2_out, Or_out, shifter_1_out, subtractor_1_out;

  assign And_out = ALU_input_1 & ALU_input_2;  // AND_Gate And, 24 bits wide
  assign Or_out = ALU_input_1 | ALU_input_2;  // OR_Gate Or, 24 bits wide
  Subtractor #(.width(24)) subtractor_1 (
    .a(ALU_input_1), .b(ALU_input_2), .out(subtractor_1_out), .bout(subtractor_1_bout));  // open: bin
  Adder #(.width(24)) adder_1 (.a(ALU_input_1), .b(ALU_input_2), .out(adder_1_out), .cin(1'b0));  // open: cout
  Shifter #(.width(24)) shifter_1 (.in(ALU_input_2), .\dist (5'b00100), .out(shifter_1_out));
  assign bit_extender_1_out = {{23{subtractor_1_bout}}, subtractor_1_bout};  // Bit_Extender bit_extender_1
  assign bit_extender_2_out = {{23{1'b0}}, subtractor_1_bout};  // Bit_Extender bit_extender_2
  assign not_1_out = ~bit_extender_1_out;  // NOT_Gate not_1, 24 bits wide
  assign and_2_out = ALU_input_1 & not_1_out;  // AND_Gate and_2, 24 bits wide
  assign and_3_out = bit_extender_1_out & ALU_input_2;  // AND_Gate and_3, 24 bits wide
  assign or_2_out = and_2_out | and_3_out;  // OR_Gate or_2, 24 bits wide
  Multiplexer #(.select(3), .width(24), .enable("false")) multiplexer_1 (
    .in0(And_out), .in1(Or_out), .in2(or_2_out), .in3(adder_1_out), .in4(subtractor_1_out),
    .in5(bit_extender_2_out), .in6(shifter_1_out), .in7({24{1'b0}}), .out(ALU_Output), .sel(ALUCtrl));
  nor nor_1 (Zero_Flag, ALU_Output[12], ALU_Output[23], ALU_Output[22], ALU_Output[21], ALU_Output[20], ALU_Output[19], ALU_Output[18], ALU_Output[17], ALU_Output[16], ALU_Output[15], ALU_Output[14], ALU_Output[13], ALU_Output[11], ALU_Output[10], ALU_Output[9], ALU_Output[8], ALU_Output[7], ALU_Output[6], ALU_Output[5], ALU_Output[4], ALU_Output[3], ALU_Output[2], ALU_Output[1], ALU_Output[0]);
endmodule

module ALU_Control (
  input  [3:0] OP,
  input  [2:0] Funct,
  output [2:0] ALUCtrl
);

  wire and_1_out, and_2_out, and_3_out, and_4_out, and_5_out, and_6_out, and_7_out, decoder_1_out0,
       decoder_1_out1, decoder_1_out2, decoder_1_out3, decoder_1_out4, decoder_1_out5, decoder_1_out6,
       decoder_1_out7, decoder_1_out8, decoder_1_out9, decoder_1_out10, decoder_1_out11, decoder_1_out12,
       decoder_2_out0, decoder_2_out1, decoder_2_out2, decoder_2_out3, decoder_2_out4, decoder_2_out5,
       decoder_2_out6, decoder_2_out7, or_1_out, or_2_out, or_3_out, or_4_out;

  Decoder #(.select(4), .enable("false")) decoder_1 (
    .out0(decoder_1_out0), .out1(decoder_1_out1), .out2(decoder_1_out2), .out3(decoder_1_out3),
    .out4(decoder_1_out4), .out5(decoder_1_out5), .out6(decoder_1_out6), .out7(decoder_1_out7),
    .out8(decoder_1_out8), .out9(decoder_1_out9), .out10(decoder_1_out10), .out11(decoder_1_out11),
    .out12(decoder_1_out12), .sel(OP));  // open: out13, out14, out15
  Decoder #(.select(3), .enable("false")) decoder_2 (
    .out0(decoder_2_out0), .out1(decoder_2_out1), .out2(decoder_2_out2), .out3(decoder_2_out3),
    .out4(decoder_2_out4), .out5(decoder_2_out5), .out6(decoder_2_out6), .out7(decoder_2_out7), .sel(Funct));
  and and_1 (and_1_out, decoder_2_out7, decoder_1_out0);
  and and_2 (and_2_out, decoder_2_out6, decoder_1_out0);
  and and_3 (and_3_out, decoder_2_out5, decoder_1_out0);
  and and_4 (and_4_out, decoder_2_out4, decoder_1_out0);
  and and_5 (and_5_out, decoder_2_out3, decoder_1_out0);
  and and_6 (and_6_out, decoder_1_out0, decoder_2_out1);
  and and_7 (and_7_out, decoder_1_out0, decoder_2_out2);
  or or_1 (or_1_out, and_1_out, decoder_1_out1);
  or or_2 (or_2_out, and_2_out, decoder_1_out2);
  or or_3 (or_3_out, and_7_out, decoder_1_out9);
  or or_4 (or_4_out, and_4_out, and_5_out, decoder_1_out3, decoder_1_out4, decoder_1_out5, decoder_1_out6, decoder_1_out7, decoder_1_out8);
  Priority_Encoder priority_encoder_1 (
    .in0(or_1_out), .in1(or_2_out), .in2(and_3_out), .in3(or_4_out), .in4(or_3_out), .in5(and_6_out),
    .in6(decoder_1_out12), .out(ALUCtrl));  // open: in7, en_in, gs, en_out

  // Notes on the sheet:
  //   R-type
  //   ANDI
  //   ORI
  //   OR
  //   CAS
  //   LWS
  //   ADD
  //   Doesn't Use
  //   AND
  //   CAS_Operation
  //   SUBTRACTION_Operation
  //   LUI
  //   AND_Operation
  //   OR_Operaion
  //   ADD_Operation
endmodule

module Control_Unit (
  input  zero,
  input  [3:0] OP,
  input  [1:0] Cond,
  output Lws,
  output JR,
  output Lw,
  output BEQ,
  output J,
  output MemToReg,
  output [1:0] RegDst,
  output ExtOP,
  output RegWrite,
  output ALUSrc,
  output MemRead,
  output MemWrite,
  output JAL,
  output LUI,
  output [2:0] ALUCtrl
);

  wire decoder_1_out0, decoder_1_out3, decoder_1_out4, decoder_1_out7, decoder_1_out8, decoder_1_out10,
       or_1_out, or_2_out, or_3_out, or_4_out, or_5_out, or_7_out, priority_encoder_1_p2,
       priority_encoder_1_p6;
  wire [3:0] and_1_out, and_2_out, multiplexer_1_out, not_2_out;

  or or_1 (or_1_out, decoder_1_out8, decoder_1_out0);
  or or_2 (or_2_out, decoder_1_out10, Lw, decoder_1_out8, decoder_1_out3, Lws);
  or or_3 (or_3_out, BEQ, decoder_1_out4);
  // Priority_Encoder priority_encoder_1: pin names not known; wires that end beside it: or_1_out, priority_encoder_1_p2, or_2_out, ALUCtrl, or_3_out, priority_encoder_1_p6, LUI
  assign and_1_out = OP & {4{zero}};  // AND_Gate and_1, 4 bits wide
  Multiplexer #(.select(2), .width(4)) multiplexer_1 (
    .in0(OP), .in1(and_1_out), .in2(and_2_out), .out(multiplexer_1_out), .sel(Cond), .en(1'b1));  // open: in3
  or or_4 (or_4_out, JAL, LUI);
  not not_1 (RegDst[1], or_4_out);
  assign not_2_out = ~{4{zero}};  // NOT_Gate not_2, 4 bits wide
  assign and_2_out = OP & not_2_out;  // AND_Gate and_2, 4 bits wide
  or or_5 (or_5_out, decoder_1_out7, decoder_1_out8, Lw, LUI);
  not not_3 (RegDst[0], or_5_out);
  or or_6 (ExtOP, decoder_1_out7, decoder_1_out8, Lw, decoder_1_out10);
  or or_7 (or_7_out, priority_encoder_1_p6, JR, decoder_1_out10, BEQ, J);
  not not_4 (RegWrite, or_7_out);
  or or_8 (ALUSrc, decoder_1_out7, decoder_1_out8, decoder_1_out10, BEQ, LUI);
  Decoder #(.select(4)) decoder_1 (
    .out0(decoder_1_out0), .out1(priority_encoder_1_p2), .out2(Lws), .out3(decoder_1_out3),
    .out4(decoder_1_out4), .out5(priority_encoder_1_p6), .out6(JR), .out7(decoder_1_out7),
    .out8(decoder_1_out8), .out9(Lw), .out10(decoder_1_out10), .out11(BEQ), .out12(J), .out13(JAL),
    .out14(LUI), .sel(multiplexer_1_out));  // open: out15, en
  or or_9 (MemRead, Lws, Lw);

  assign MemToReg = MemRead;
  assign MemWrite = J;
endmodule

module Next_PC (
  input  [16:0] Imm,
  input  [23:0] inc_PC,
  input  Zero_Flag,
  input  BEQ,
  input  J,
  input  JR,
  input  JAL,
  input  [23:0] BusA,
  output PCSrc,
  output [23:0] J_JAL_BEQ_NEW_ADD
);

  wire and_1_out, or_1_out;
  wire [23:0] adder_1_out, bit_extender_1_out, multiplexer_1_out, shifter_1_out, undriven;

  assign bit_extender_1_out = {{14{Imm[9]}}, Imm[9:0]};  // Bit_Extender bit_extender_1
  Shifter #(.width(24)) shifter_1 (.in(bit_extender_1_out), .\dist (5'b00001), .out(shifter_1_out));
  Adder #(.width(24)) adder_1 (.a(shifter_1_out), .b(inc_PC), .out(adder_1_out));  // open: cin, cout
  Multiplexer #(.width(24), .enable("false")) multiplexer_1 (
    .in0(adder_1_out), .in1(undriven), .out(multiplexer_1_out), .sel(or_1_out));
  or or_1 (or_1_out, J, JAL);
  Multiplexer #(.width(24), .enable("false")) multiplexer_2 (
    .in0(multiplexer_1_out), .in1(BusA), .out(J_JAL_BEQ_NEW_ADD), .sel(JR));
  or or_2 (PCSrc, and_1_out, J, JR, JAL);
  and and_1 (and_1_out, Zero_Flag, BEQ);

  // Notes on the sheet:
  //   Branch
  //   J,JAL
endmodule

module Data_Memory (
  input  [23:0] Address,
  input  [23:0] Data_In,
  input  clk,
  input  MemWrite,
  input  MemRead,
  output [23:0] Data_Out
);

  RAM #(.addrWidth(24), .dataWidth(24), .bus("separate")) ram_1 (
    .addr(Address), .din(Data_In), .data(Data_Out), .str(MemWrite), .clk(clk), .ld(MemRead), .clr(1'b0));  // open: sel
endmodule

// INC_PC
module Inc_PC (
  input  [23:0] PC,
  input  enable,
  input  clk,
  output [23:0] PCToInsMem,
  output [23:0] IncPC
);

  Register #(.width(24)) register_1 (.D(PC), .en(enable), .Q(PCToInsMem), .clk(clk));  // open: clr
  Adder #(.width(24)) adder_1 (.a(PCToInsMem), .b(24'h2), .out(IncPC));  // open: cin, cout
endmodule

// IF/ID
module IF_ID_Buffer (
  input  Clear,
  input  [23:0] Fetched_Inst,
  input  [23:0] Incremented_PC,
  input  clock,
  input  Enable,
  output [2:0] Rd,
  output [2:0] Rt,
  output [2:0] Rs,
  output Sf,
  output [3:0] Op,
  output [23:0] Inc_Pc,
  output [1:0] Cond,
  output [9:0] Imm_10,
  output [16:0] Imm_17
);

  wire [21:21] IR_q;
  wire [23:0] multiplexer_1_out;

  Multiplexer #(.width(24), .enable("false")) multiplexer_1 (
    .in0(Fetched_Inst), .in1({24{1'b1}}), .out(multiplexer_1_out), .sel(Clear));
  Register #(.width(24)) IR (
    .D(multiplexer_1_out), .en(Enable), .Q({Cond, IR_q[21], Op, Imm_17[16:10], Imm_10}), .clk(clock));  // open: clr
  Register #(.width(24)) u_Inc_PC (.D(Incremented_PC), .en(Enable), .Q(Inc_Pc), .clk(clock));  // open: clr

  assign Imm_17[9:0] = Imm_10;
  assign Rd = Imm_10[9:7];
  assign Rs = Imm_17[15:13];
  assign Rt = Imm_17[12:10];
  assign Sf = Imm_17[16];
endmodule

module Pipeline_Circuit (
  input  in_1,
  input  in_2
);

  wire alu_1_zero_flag, ALUSrc1, ALUSrc2, BEQ1, BusA1, BusA2, BusA3, BusB1, BusB2, BusB3, ExtOP1, FLUSH_ID,
       FLUSH_IF, forwarding_wb_to_mem_1_store_data, J1, JAL1, JAL2, JR1, LUI1, LUI2, Lw1, Lw2, Lw3, Lws1,
       Lws2, Lws3, MEM_to_EX_ALU1, MEM_to_EX_ALU2, MemRead1, MemRead2, MemRead3, MemToReg1, MemToReg2,
       MemToReg3, MemToReg4, MemWrite1, MemWrite2, MemWrite3, not_1_out, not_2_out, not_3_out, not_4_out,
       PCSrc, RegWrite1, RegWrite2, RegWrite3, RegWrite4, SF, Stall_IF_ID, WB_to_EX_ALU1, WB_to_EX_ALU2, Zero;
  wire [1:0] if_id_buffer_1_cond, RegDst, RegDst2;
  wire [2:0] ALUCtrl, control_unit_1_aluctrl, ex_mem_1_rt_2, ex_mem_1_rw_2, id_ex_buffer_1_rd_2,
       id_ex_buffer_1_rt_2, ID_EX_RS, if_id_buffer_1_rd, if_id_buffer_1_rs, if_id_buffer_1_rt, mem_wb_1_rw_2,
       multiplexer_10_out, multiplexer_12_out;
  wire [3:0] if_id_buffer_1_op, rom_1_data, rom_1_data_2, rom_1_data_3, rom_1_data_4, rom_1_data_5,
       rom_1_data_6;
  wire [9:0] if_id_buffer_1_imm_10;
  wire [16:0] if_id_buffer_1_imm_17;
  wire [23:0] alu_1_alu_output, ALU_IN1, ALU_IN2, ex_mem_1_busb_2, EX_MEM_ALUres, EX_MEM_MemRes,
       extender_10_1_imm_16, extender_17_1_imm_24, FinalResBUSB, ID_EX_ALURes, id_ex_buffer_1_busa_2,
       id_ex_buffer_1_busb_2, id_ex_buffer_1_imm_itype_2, id_ex_buffer_1_imm_jtype_2, if_id_buffer_1_inc_pc,
       inc_pc_1_incpc, inc_pc_1_pctoinsmem, IncPC2, IncPC3, mem_wb_1_aluresult_2, mem_wb_1_memorydata_2,
       Memory_Data, multiplexer_1_out, multiplexer_2_out, multiplexer_3_out, multiplexer_4_out,
       multiplexer_5_out, multiplexer_6_out, multiplexer_8_out, multiplexer_9_out, multiplexer_11_out,
       multiplexer_14_out, next_pc_1_j_jal_beq_new_add, register_file_1_busa, register_file_1_busb,
       WB_to_EX_res;

  Multiplexer #(.width(24), .enable("false")) multiplexer_1 (
    .in0(inc_pc_1_incpc), .in1(next_pc_1_j_jal_beq_new_add), .out(multiplexer_1_out), .sel(PCSrc));
  not not_1 (not_1_out, Stall_IF_ID);
  Hazard_Detection hazard_detection_1 (
    .clk(in_2), .ID_EX_MemRead(MemRead2), .ID_EX_RegisterRd(multiplexer_12_out),
    .IF_ID_RegisterRs(if_id_buffer_1_rs), .IF_ID_MemWrite(MemWrite1), .IF_ID_RegisterRt(if_id_buffer_1_rt),
    .Flush_IF(FLUSH_IF), .Flush_ID(FLUSH_ID), .Stall_ID_Stall_IF(Stall_IF_ID), .PCsrc(PCSrc),
    .PC1(next_pc_1_j_jal_beq_new_add), .PC2(inc_pc_1_incpc));
  Hex_Digit_Display hex_digit_display_1 (.value(rom_1_data_6));  // open: dp
  Hex_Digit_Display hex_digit_display_2 (.value(rom_1_data_5));  // open: dp
  Inc_PC inc_pc_1 (
    .PC(multiplexer_1_out), .PCToInsMem(inc_pc_1_pctoinsmem), .IncPC(inc_pc_1_incpc), .clk(in_2),
    .enable(not_1_out));
  Hex_Digit_Display hex_digit_display_3 (.value(rom_1_data_4));  // open: dp
  Hex_Digit_Display hex_digit_display_4 (.value(rom_1_data_3));  // open: dp
  Hex_Digit_Display hex_digit_display_5 (.value(rom_1_data));  // open: dp
  Hex_Digit_Display hex_digit_display_6 (.value(rom_1_data_2));  // open: dp
  ROM #(.addrWidth(24), .dataWidth(24)) rom_1 (
    .addr(inc_pc_1_pctoinsmem),
    .data({rom_1_data_6, rom_1_data_5, rom_1_data_4, rom_1_data_3, rom_1_data_2, rom_1_data}));  // open: sel
  not not_2 (not_2_out, Stall_IF_ID);
  IF_ID_Buffer if_id_buffer_1 (
    .Fetched_Inst({rom_1_data_6, rom_1_data_5, rom_1_data_4, rom_1_data_3, rom_1_data_2, rom_1_data}),
    .Incremented_PC(inc_pc_1_incpc), .clock(in_2), .Inc_Pc(if_id_buffer_1_inc_pc), .Enable(not_2_out),
    .Clear(FLUSH_IF), .Imm_17(if_id_buffer_1_imm_17), .Op(if_id_buffer_1_op), .Cond(if_id_buffer_1_cond),
    .Sf(SF), .Rs(if_id_buffer_1_rs), .Rt(if_id_buffer_1_rt), .Rd(if_id_buffer_1_rd),
    .Imm_10(if_id_buffer_1_imm_10));
  Control_Unit control_unit_1 (
    .OP(if_id_buffer_1_op), .ALUCtrl(control_unit_1_aluctrl), .RegDst(RegDst), .ExtOP(ExtOP1),
    .RegWrite(RegWrite1), .ALUSrc(ALUSrc1), .MemRead(MemRead1), .MemWrite(MemWrite1), .Lws(Lws1), .JR(JR1),
    .Lw(Lw1), .BEQ(BEQ1), .J(J1), .JAL(JAL1), .LUI(LUI1), .MemToReg(MemToReg1), .Cond(if_id_buffer_1_cond),
    .zero(alu_1_zero_flag));
  not not_3 (not_3_out, in_2);
  Register_File register_file_1 (
    .BusW(WB_to_EX_res), .RW(mem_wb_1_rw_2), .BusA(register_file_1_busa), .BusB(register_file_1_busb),
    .RegWrite(RegWrite4), .RA(if_id_buffer_1_rs), .RB(if_id_buffer_1_rt), .Clock(not_3_out));
  Extender_10 extender_10_1 (._6_bit_immediate(if_id_buffer_1_imm_10), .Imm_16(extender_10_1_imm_16), .ExtOP(ExtOP1));
  Extender_17 extender_17_1 (.Imm_17(if_id_buffer_1_imm_17), .Imm_24(extender_17_1_imm_24));
  Next_PC next_pc_1 (
    .Imm(if_id_buffer_1_imm_17), .inc_PC(if_id_buffer_1_inc_pc),
    .J_JAL_BEQ_NEW_ADD(next_pc_1_j_jal_beq_new_add), .PCSrc(PCSrc), .BusA(multiplexer_6_out),
    .Zero_Flag(Zero), .BEQ(BEQ1), .J(J1), .JR(JR1), .JAL(JAL1));
  Multiplexer #(.width(24), .enable("false")) multiplexer_2 (
    .in0(register_file_1_busa), .in1(ID_EX_ALURes), .out(multiplexer_2_out), .sel(BusA1));
  Multiplexer #(.width(24), .enable("false")) multiplexer_3 (
    .in0(register_file_1_busb), .in1(ID_EX_ALURes), .out(multiplexer_3_out), .sel(BusB1));
  Forwarding_EX_to_ID forwarding_ex_to_id_1 (
    .ID_EX_RegWrite(RegWrite2), .for_RS(BusA1), .for_RT(BusB1), .ID_EX_RegisterRd(multiplexer_12_out),
    .IF_ID_RegisterRs(if_id_buffer_1_rs), .IF_ID_RegisterRt(if_id_buffer_1_rt), .ID_EX_MemRead(MemRead2));
  Forwarding_ALURes_MEM_to_ID forwarding_alures_mem_to_id_1 (
    .BusA(BusA3), .BusB(BusB3), .Ex_Mem_RegWrite(RegWrite3), .Ex_MEM_RegisterRd(ex_mem_1_rw_2),
    .IF_ID_RegisterRs(if_id_buffer_1_rs), .IF_ID_Rt_RegisterRt(if_id_buffer_1_rt),
    .ID_EX_RegisterRd(multiplexer_12_out), .EX_MEM_MemRead(MemRead3));
  Hex_Digit_Display hex_digit_display_7 (.value(next_pc_1_j_jal_beq_new_add[23:20]));  // open: dp
  Multiplexer #(.width(24), .enable("false")) multiplexer_4 (
    .in0(multiplexer_2_out), .in1(EX_MEM_MemRes), .out(multiplexer_4_out), .sel(BusA2));
  Multiplexer #(.width(24), .enable("false")) multiplexer_5 (
    .in0(multiplexer_3_out), .in1(EX_MEM_MemRes), .out(multiplexer_5_out), .sel(BusB2));
  Forwarding_MEM_to_ID forwarding_mem_to_id_1 (
    .EX_MEM_MemRead(MemRead3), .BusA(BusA2), .BusB(BusB2), .Ex_MEM_RegisterRd(ex_mem_1_rw_2),
    .Ex_Mem_RegWrite(RegWrite3), .IF_ID_RegisterRs(if_id_buffer_1_rs), .ID_EX_RegisterRd(multiplexer_12_out),
    .IF_ID_Rt_RegisterRt(if_id_buffer_1_rt));
  Hex_Digit_Display hex_digit_display_8 (.value(FinalResBUSB[19:16]));  // open: dp
  Hex_Digit_Display hex_digit_display_9 (.value(FinalResBUSB[23:20]));  // open: dp
  Hex_Digit_Display hex_digit_display_10 (.value(next_pc_1_j_jal_beq_new_add[15:12]));  // open: dp
  Hex_Digit_Display hex_digit_display_11 (.value(next_pc_1_j_jal_beq_new_add[19:16]));  // open: dp
  Hex_Digit_Display hex_digit_display_12 (.value(multiplexer_6_out[19:16]));  // open: dp
  Hex_Digit_Display hex_digit_display_13 (.value(multiplexer_6_out[23:20]));  // open: dp
  Multiplexer #(.width(24), .enable("false")) multiplexer_6 (
    .in0(multiplexer_4_out), .in1(EX_MEM_ALUres), .out(multiplexer_6_out), .sel(BusA3));
  Comparator #(.width(24)) comparator_1 (.a(multiplexer_6_out), .b(FinalResBUSB), .eq(Zero));  // open: gt, lt
  Multiplexer #(.width(24), .enable("false")) multiplexer_7 (
    .in0(multiplexer_5_out), .in1(EX_MEM_ALUres), .out(FinalResBUSB), .sel(BusB3));
  Hex_Digit_Display hex_digit_display_14 (.value(FinalResBUSB[15:12]));  // open: dp
  Hex_Digit_Display hex_digit_display_15 (.value(FinalResBUSB[11:8]));  // open: dp
  Hex_Digit_Display hex_digit_display_16 (.value(next_pc_1_j_jal_beq_new_add[7:4]));  // open: dp
  Hex_Digit_Display hex_digit_display_17 (.value(next_pc_1_j_jal_beq_new_add[11:8]));  // open: dp
  Hex_Digit_Display hex_digit_display_18 (.value(multiplexer_6_out[15:12]));  // open: dp
  Hex_Digit_Display hex_digit_display_19 (.value(multiplexer_6_out[11:8]));  // open: dp
  Hex_Digit_Display hex_digit_display_20 (.value(FinalResBUSB[3:0]));  // open: dp
  Hex_Digit_Display hex_digit_display_21 (.value(FinalResBUSB[7:4]));  // open: dp
  Hex_Digit_Display hex_digit_display_22 (.value(next_pc_1_j_jal_beq_new_add[3:0]));  // open: dp
  Hex_Digit_Display hex_digit_display_23 (.value(multiplexer_6_out[7:4]));  // open: dp
  Hex_Digit_Display hex_digit_display_24 (.value(multiplexer_6_out[3:0]));  // open: dp
  ID_EX_Buffer id_ex_buffer_1 (
    .BusA(multiplexer_6_out), .BusB(FinalResBUSB), .imm_Itype(extender_10_1_imm_16),
    .imm_Jtype(extender_17_1_imm_24), .Rt(if_id_buffer_1_rt), .Rd(if_id_buffer_1_rd), .MemToReg(MemToReg1),
    .RegWrite(RegWrite1), .MemRead(MemRead1), .MemWrite(MemWrite1), .ALUSrc(ALUSrc1), .JAL(JAL1), .LUI(LUI1),
    .RegDst(RegDst), .clock(in_2), .BusA_2(id_ex_buffer_1_busa_2), .BusB_2(id_ex_buffer_1_busb_2),
    .imm_Itype_2(id_ex_buffer_1_imm_itype_2), .imm_Jtype_2(id_ex_buffer_1_imm_jtype_2),
    .Rt_2(id_ex_buffer_1_rt_2), .Rd_2(id_ex_buffer_1_rd_2), .MemToReg_2(MemToReg2), .RegWrite_2(RegWrite2),
    .MemRead_2(MemRead2), .MemWrite_2(MemWrite2), .ALUSrc_2(ALUSrc2), .JAL_2(JAL2), .LUI_2(LUI2),
    .RegDst_2(RegDst2), .OP(if_id_buffer_1_op), .AluCtrl(control_unit_1_aluctrl), .AluCtrl_2(ALUCtrl),
    .IncPC(if_id_buffer_1_inc_pc), .IncPC_2(IncPC2), .RS(if_id_buffer_1_rs), .RS_2(ID_EX_RS), .Enable(1'b1),
    .Clear(FLUSH_ID), .Lw(Lw1), .Lw_2(Lw2), .Lws(Lws1), .Lws_2(Lws2));  // open: OP_2
  Hex_Digit_Display hex_digit_display_25 (.value(ALU_IN1[19:16]));  // open: dp
  Hex_Digit_Display hex_digit_display_26 (.value(ALU_IN1[23:20]));  // open: dp
  Multiplexer #(.width(24), .enable("false")) multiplexer_8 (
    .in0(id_ex_buffer_1_busa_2), .in1(EX_MEM_ALUres), .out(multiplexer_8_out), .sel(MEM_to_EX_ALU1));
  Multiplexer #(.width(24), .enable("false")) multiplexer_9 (
    .in0(id_ex_buffer_1_imm_itype_2), .in1(id_ex_buffer_1_imm_jtype_2), .out(multiplexer_9_out), .sel(LUI2));
  Multiplexer #(.select(2), .width(3), .enable("false")) multiplexer_10 (
    .in0(3'b001), .in1(3'b111), .in2(id_ex_buffer_1_rt_2), .in3(id_ex_buffer_1_rd_2),
    .out(multiplexer_10_out), .sel(RegDst2));
  Hex_Digit_Display hex_digit_display_27 (.value(ALU_IN1[11:8]));  // open: dp
  Hex_Digit_Display hex_digit_display_28 (.value(ALU_IN1[15:12]));  // open: dp
  Hex_Digit_Display hex_digit_display_29 (.value(ALU_IN2[23:20]));  // open: dp
  Multiplexer #(.width(24), .enable("false")) multiplexer_11 (
    .in0(id_ex_buffer_1_busb_2), .in1(EX_MEM_ALUres), .out(multiplexer_11_out), .sel(MEM_to_EX_ALU2));
  Multiplexer #(.width(3), .enable("false")) multiplexer_12 (
    .in0(3'b000), .in1(multiplexer_10_out), .out(multiplexer_12_out), .sel(RegWrite2));
  MEM_to_EX mem_to_ex_1 (
    .MEM_to_EX_ALU1(MEM_to_EX_ALU1), .MEM_to_EX_ALU2(MEM_to_EX_ALU2), .EX_MEM_RegisterRd(ex_mem_1_rw_2),
    .EX_MEM_RegWrite(RegWrite3), .ID_EX_RegisterRs(ID_EX_RS), .ID_EX_RegisterRt(id_ex_buffer_1_rt_2));
  Hex_Digit_Display hex_digit_display_30 (.value(ALU_IN1[7:4]));  // open: dp
  Hex_Digit_Display hex_digit_display_31 (.value(ALU_IN1[3:0]));  // open: dp
  Hex_Digit_Display hex_digit_display_32 (.value(ALU_IN2[19:16]));  // open: dp
  Hex_Digit_Display hex_digit_display_33 (.value(ALU_IN2[15:12]));  // open: dp
  Multiplexer #(.width(24), .enable("false")) multiplexer_13 (
    .in0(multiplexer_8_out), .in1(WB_to_EX_res), .out(ALU_IN1), .sel(WB_to_EX_ALU1));
  Multiplexer #(.width(24), .enable("false")) multiplexer_14 (
    .in0(multiplexer_11_out), .in1(WB_to_EX_res), .out(multiplexer_14_out), .sel(WB_to_EX_ALU2));
  Hex_Digit_Display hex_digit_display_34 (.value(ALU_IN2[11:8]));  // open: dp
  Hex_Digit_Display hex_digit_display_35 (.value(ALU_IN2[7:4]));  // open: dp
  Multiplexer #(.width(24), .enable("false")) multiplexer_15 (
    .in0(multiplexer_14_out), .in1(multiplexer_9_out), .out(ALU_IN2), .sel(ALUSrc2));
  Hex_Digit_Display hex_digit_display_36 (.value(ALU_IN2[3:0]));  // open: dp
  Forwarding_WB_to_EX forwarding_wb_to_ex_1 (
    .ALU1(WB_to_EX_ALU1), .ALU2(WB_to_EX_ALU2), .MEM_WB_RegisterRd(mem_wb_1_rw_2),
    .MEM_WB_RegWrite(RegWrite4), .ID_EX_RegisterRs(ID_EX_RS), .EX_MEM_RegisterRd(ex_mem_1_rw_2),
    .ID_EX_RegisterRt(id_ex_buffer_1_rt_2));
  Hex_Digit_Display hex_digit_display_37 (.value(ID_EX_ALURes[23:20]));  // open: dp
  Hex_Digit_Display hex_digit_display_38 (.value(ID_EX_ALURes[19:16]));  // open: dp
  ALU alu_1 (
    .ALU_input_1(ALU_IN1), .ALU_Output(alu_1_alu_output), .ALUCtrl(ALUCtrl), .ALU_input_2(ALU_IN2),
    .Zero_Flag(alu_1_zero_flag));
  Hex_Digit_Display hex_digit_display_39 (.value(ID_EX_ALURes[15:12]));  // open: dp
  Hex_Digit_Display hex_digit_display_40 (.value(ID_EX_ALURes[11:8]));  // open: dp
  Hex_Digit_Display hex_digit_display_41 (.value(ID_EX_ALURes[3:0]));  // open: dp
  Hex_Digit_Display hex_digit_display_42 (.value(ID_EX_ALURes[7:4]));  // open: dp
  Multiplexer #(.width(24), .enable("false")) multiplexer_16 (
    .in0(alu_1_alu_output), .in1(IncPC2), .out(ID_EX_ALURes), .sel(JAL2));
  EX_MEM ex_mem_1 (
    .ALUResult(ID_EX_ALURes), .IncPC(IncPC2), .RW(multiplexer_12_out), .BusB(id_ex_buffer_1_busb_2),
    .MemToReg(MemToReg2), .RegWrite(RegWrite2), .MemRead(MemRead2), .MemWrite(MemWrite2), .clock(in_2),
    .ALUResult_2(EX_MEM_ALUres), .IncPC_2(IncPC3), .RW_2(ex_mem_1_rw_2), .BusB_2(ex_mem_1_busb_2),
    .MemToReg_2(MemToReg3), .RegWrite_2(RegWrite3), .MemRead_2(MemRead3), .MemWrite_2(MemWrite3),
    .RT(id_ex_buffer_1_rt_2), .RT_2(ex_mem_1_rt_2), .Enable(1'b1), .Clear(1'b0), .Lb_2(Lw3), .Lbu_2(Lws3),
    .Lbu(Lws2), .Lb(Lw2));
  Multiplexer #(.width(24), .enable("false")) multiplexer_17 (
    .in0(ex_mem_1_busb_2), .in1(WB_to_EX_res), .out(Memory_Data), .sel(forwarding_wb_to_mem_1_store_data));
  Hex_Digit_Display hex_digit_display_43 (.value(Memory_Data[23:20]));  // open: dp
  Forwarding_WB_to_MEM forwarding_wb_to_mem_1 (
    .MEM_WB_RegisterRd(mem_wb_1_rw_2), .Store_Data(forwarding_wb_to_mem_1_store_data),
    .MEM_WB_RegWrite(RegWrite4), .EX_MEM_RegisterRt(ex_mem_1_rt_2));
  Hex_Digit_Display hex_digit_display_44 (.value(EX_MEM_ALUres[19:16]));  // open: dp
  Hex_Digit_Display hex_digit_display_45 (.value(EX_MEM_ALUres[23:20]));  // open: dp
  not not_4 (not_4_out, in_2);
  Hex_Digit_Display hex_digit_display_46 (.value(Memory_Data[19:16]));  // open: dp
  Hex_Digit_Display hex_digit_display_47 (.value(Memory_Data[15:12]));  // open: dp
  Hex_Digit_Display hex_digit_display_48 (.value(EX_MEM_ALUres[15:12]));  // open: dp
  Hex_Digit_Display hex_digit_display_49 (.value(EX_MEM_ALUres[11:8]));  // open: dp
  RAM #(.addrWidth(24), .dataWidth(24), .bus("separate")) ram_1 (
    .addr(EX_MEM_ALUres), .din(Memory_Data), .data(EX_MEM_MemRes), .str(MemWrite3), .clk(not_4_out),
    .ld(MemRead3));  // open: sel, clr
  Hex_Digit_Display hex_digit_display_50 (.value(Memory_Data[7:4]));  // open: dp
  Hex_Digit_Display hex_digit_display_51 (.value(Memory_Data[11:8]));  // open: dp
  Hex_Digit_Display hex_digit_display_52 (.value(EX_MEM_MemRes[19:16]));  // open: dp
  Hex_Digit_Display hex_digit_display_53 (.value(EX_MEM_MemRes[23:20]));  // open: dp
  Hex_Digit_Display hex_digit_display_54 (.value(EX_MEM_ALUres[7:4]));  // open: dp
  Hex_Digit_Display hex_digit_display_55 (.value(EX_MEM_ALUres[3:0]));  // open: dp
  Hex_Digit_Display hex_digit_display_56 (.value(Memory_Data[3:0]));  // open: dp
  Hex_Digit_Display hex_digit_display_57 (.value(EX_MEM_MemRes[11:8]));  // open: dp
  Hex_Digit_Display hex_digit_display_58 (.value(EX_MEM_MemRes[15:12]));  // open: dp
  Hex_Digit_Display hex_digit_display_59 (.value(EX_MEM_MemRes[7:4]));  // open: dp
  Hex_Digit_Display hex_digit_display_60 (.value(EX_MEM_MemRes[3:0]));  // open: dp
  MEM_WB mem_wb_1 (
    .ALUResult(EX_MEM_ALUres), .IncPC(IncPC3), .MemoryData(EX_MEM_MemRes), .MemToReg(MemToReg3),
    .RegWrite(RegWrite3), .RW(ex_mem_1_rw_2), .clock(in_2), .ALUResult_2(mem_wb_1_aluresult_2),
    .MemoryData_2(mem_wb_1_memorydata_2), .MemToReg_2(MemToReg4), .RegWrite_2(RegWrite4),
    .RW_2(mem_wb_1_rw_2), .Enable(1'b1), .Clear(1'b0));  // open: IncPC_2
  Hex_Digit_Display hex_digit_display_61 (.value(WB_to_EX_res[19:16]));  // open: dp
  Hex_Digit_Display hex_digit_display_62 (.value(WB_to_EX_res[23:20]));  // open: dp
  Multiplexer #(.width(24), .enable("false")) multiplexer_18 (
    .in0(mem_wb_1_aluresult_2), .in1(mem_wb_1_memorydata_2), .out(WB_to_EX_res), .sel(MemToReg4));
  Hex_Digit_Display hex_digit_display_63 (.value(WB_to_EX_res[11:8]));  // open: dp
  Hex_Digit_Display hex_digit_display_64 (.value(WB_to_EX_res[15:12]));  // open: dp
  Hex_Digit_Display hex_digit_display_65 (.value(WB_to_EX_res[7:4]));  // open: dp
  Hex_Digit_Display hex_digit_display_66 (.value(WB_to_EX_res[3:0]));  // open: dp

  // Other names for the same wires on the sheet: Clk = in_2

  // Notes on the sheet:
  //   Fetched_Instruction
  //   contents of rom_1 (hex, n*v repeats v):
  //   111111 0 ffb002
  //   EX/EME.Rd
  //   BUSB
  //   Next_PC
  //   BUS A
  //   ALU IN 1
  //   ALU IN 2
  //   ALU Result
  //   ALU Result in Mem Stage
  //   Final Result
endmodule

module Extender_17 (
  input  [16:0] Imm_17,
  output [23:0] Imm_24
);

  assign Imm_24 = {{7{Imm_17[16]}}, Imm_17};  // Bit_Extender bit_extender_1
endmodule

module Extender_10 (
  input  [9:0] _6_bit_immediate,
  input  ExtOP,
  output [23:0] Imm_16
);

  wire [23:0] bit_extender_1_out, bit_extender_2_out;

  assign bit_extender_1_out = {{14{1'b0}}, _6_bit_immediate};  // Bit_Extender bit_extender_1
  assign bit_extender_2_out = {{14{_6_bit_immediate[9]}}, _6_bit_immediate};  // Bit_Extender bit_extender_2
  Multiplexer #(.width(24)) multiplexer_1 (
    .in0(bit_extender_1_out), .in1(bit_extender_2_out), .out(Imm_16), .sel(ExtOP));  // open: en
endmodule

// ID/EX
module ID_EX_Buffer (
  input  [23:0] BusA,
  input  [23:0] BusB,
  input  [23:0] imm_Itype,
  input  [23:0] imm_Jtype,
  input  [2:0] Rt,
  input  [2:0] Rd,
  input  MemToReg,
  input  RegWrite,
  input  MemRead,
  input  MemWrite,
  input  ALUSrc,
  input  JAL,
  input  LUI,
  input  [1:0] RegDst,
  input  [3:0] OP,
  input  [2:0] AluCtrl,
  input  [23:0] IncPC,
  input  [2:0] RS,
  input  Lw,
  input  Lws,
  input  clock,
  input  Enable,
  input  Clear,
  output [23:0] BusA_2,
  output [23:0] BusB_2,
  output [23:0] imm_Itype_2,
  output [23:0] imm_Jtype_2,
  output [2:0] Rt_2,
  output [2:0] Rd_2,
  output MemToReg_2,
  output RegWrite_2,
  output MemRead_2,
  output MemWrite_2,
  output ALUSrc_2,
  output JAL_2,
  output LUI_2,
  output [1:0] RegDst_2,
  output [3:0] OP_2,
  output [2:0] AluCtrl_2,
  output [23:0] IncPC_2,
  output [2:0] RS_2,
  output Lw_2,
  output Lws_2
);

  Register #(.width(24)) register_1 (.D(IncPC), .en(Enable), .Q(IncPC_2), .clk(clock), .clr(Clear));
  Register #(.width(3)) register_2 (.D(RS), .en(Enable), .Q(RS_2), .clk(clock), .clr(Clear));
  Register #(.width(1)) Lu (.D(Lw), .en(Enable), .Q(Lw_2), .clk(clock), .clr(Clear));
  Register #(.width(1)) register_3 (.D(Lws), .en(Enable), .Q(Lws_2), .clk(clock), .clr(Clear));
  Register #(.width(24)) register_4 (.D(BusA), .en(Enable), .Q(BusA_2), .clk(clock), .clr(Clear));
  Register #(.width(24)) register_5 (.D(BusB), .en(Enable), .Q(BusB_2), .clk(clock), .clr(Clear));
  Register #(.width(24)) register_6 (.D(imm_Itype), .en(Enable), .Q(imm_Itype_2), .clk(clock), .clr(Clear));
  Register #(.width(24)) register_7 (.D(imm_Jtype), .en(Enable), .Q(imm_Jtype_2), .clk(clock), .clr(Clear));
  Register #(.width(3)) register_8 (.D(Rt), .en(Enable), .Q(Rt_2), .clk(clock), .clr(Clear));
  Register #(.width(3)) register_9 (.D(Rd), .en(Enable), .Q(Rd_2), .clk(clock), .clr(Clear));
  Register #(.width(1)) register_10 (.D(MemToReg), .en(Enable), .Q(MemToReg_2), .clk(clock), .clr(Clear));
  Register #(.width(1)) register_11 (.D(RegWrite), .en(Enable), .Q(RegWrite_2), .clk(clock), .clr(Clear));
  Register #(.width(1)) register_12 (.D(MemRead), .en(Enable), .Q(MemRead_2), .clk(clock), .clr(Clear));
  Register #(.width(1)) register_13 (.D(MemWrite), .en(Enable), .Q(MemWrite_2), .clk(clock), .clr(Clear));
  Register #(.width(1)) register_14 (.D(ALUSrc), .en(Enable), .Q(ALUSrc_2), .clk(clock), .clr(Clear));
  Register #(.width(1)) register_15 (.D(JAL), .en(Enable), .Q(JAL_2), .clk(clock), .clr(Clear));
  Register #(.width(1)) register_16 (.D(LUI), .en(Enable), .Q(LUI_2), .clk(clock), .clr(Clear));
  Register #(.width(2)) register_17 (.D(RegDst), .en(Enable), .Q(RegDst_2), .clk(clock), .clr(Clear));
  Register #(.width(4)) register_18 (.D(OP), .en(Enable), .Q(OP_2), .clk(clock), .clr(Clear));
  Register #(.width(3)) register_19 (.D(AluCtrl), .en(Enable), .Q(AluCtrl_2), .clk(clock), .clr(Clear));
endmodule

module EX_MEM (
  input  [23:0] ALUResult,
  input  [23:0] IncPC,
  input  [2:0] RW,
  input  [23:0] BusB,
  input  MemToReg,
  input  RegWrite,
  input  MemRead,
  input  MemWrite,
  input  [2:0] RT,
  input  Lb,
  input  Lbu,
  input  clock,
  input  Enable,
  input  Clear,
  output [23:0] ALUResult_2,
  output [23:0] IncPC_2,
  output [2:0] RW_2,
  output [23:0] BusB_2,
  output MemToReg_2,
  output RegWrite_2,
  output MemRead_2,
  output MemWrite_2,
  output [2:0] RT_2,
  output Lb_2,
  output Lbu_2
);

  Register #(.width(24)) register_1 (.D(ALUResult), .en(Enable), .Q(ALUResult_2), .clk(clock), .clr(Clear));
  Register #(.width(24)) register_2 (.D(IncPC), .en(Enable), .Q(IncPC_2), .clk(clock), .clr(Clear));
  Register #(.width(3)) register_3 (.D(RW), .en(Enable), .Q(RW_2), .clk(clock), .clr(Clear));
  Register #(.width(24)) register_4 (.D(BusB), .en(Enable), .Q(BusB_2), .clk(clock), .clr(Clear));
  Register #(.width(1)) register_5 (.D(MemToReg), .en(Enable), .Q(MemToReg_2), .clk(clock), .clr(Clear));
  Register #(.width(1)) register_6 (.D(RegWrite), .en(Enable), .Q(RegWrite_2), .clk(clock), .clr(Clear));
  Register #(.width(1)) register_7 (.D(MemRead), .en(Enable), .Q(MemRead_2), .clk(clock), .clr(Clear));
  Register #(.width(1)) register_8 (.D(MemWrite), .en(Enable), .Q(MemWrite_2), .clk(clock), .clr(Clear));
  Register #(.width(3)) register_9 (.D(RT), .en(Enable), .Q(RT_2), .clk(clock), .clr(Clear));
  Register #(.width(1)) register_10 (.D(Lb), .en(Enable), .Q(Lb_2), .clk(clock), .clr(Clear));
  Register #(.width(1)) register_11 (.D(Lbu), .en(Enable), .Q(Lbu_2), .clk(clock), .clr(Clear));
endmodule

module MEM_WB (
  input  [23:0] ALUResult,
  input  [23:0] IncPC,
  input  [23:0] MemoryData,
  input  MemToReg,
  input  RegWrite,
  input  [2:0] RW,
  input  clock,
  input  Enable,
  input  Clear,
  output [23:0] ALUResult_2,
  output [23:0] IncPC_2,
  output [23:0] MemoryData_2,
  output MemToReg_2,
  output RegWrite_2,
  output [2:0] RW_2
);

  Register #(.width(24)) register_1 (.D(ALUResult), .en(Enable), .Q(ALUResult_2), .clk(clock), .clr(Clear));
  Register #(.width(24)) register_2 (.D(IncPC), .en(Enable), .Q(IncPC_2), .clk(clock), .clr(Clear));
  Register #(.width(24)) register_3 (.D(MemoryData), .en(Enable), .Q(MemoryData_2), .clk(clock), .clr(Clear));
  Register #(.width(1)) register_4 (.D(MemToReg), .en(Enable), .Q(MemToReg_2), .clk(clock), .clr(Clear));
  Register #(.width(1)) register_5 (.D(RegWrite), .en(Enable), .Q(RegWrite_2), .clk(clock), .clr(Clear));
  Register #(.width(3)) register_6 (.D(RW), .en(Enable), .Q(RW_2), .clk(clock), .clr(Clear));
endmodule

module Forwarding_Unit (
  input  EX_MEM_RegWrite,
  input  MEM_WB_RegWrite,
  input  [2:0] EX_MEM_RegisterRd,
  input  [2:0] ID_EX_RegisterRs,
  input  [2:0] ID_EX_RegisterRt,
  input  [2:0] MEM_WB_RegisterRd,
  input  [2:0] ID_EX_RegisterRs_2,
  input  [2:0] ID_EX_RegisterRt_2,
  input  [2:0] EX_MEM_RegisterRd_2,
  input  MEM_WB_RegWrite_2,
  input  [2:0] MEM_WB_RegisterRd_2,
  input  [2:0] EX_MEM_RegisterRt,
  input  ID_EX_RegWrite,
  input  BEQ,
  input  JR,
  input  [2:0] ID_EX_RegisterRd,
  input  [2:0] IF_ID_RegisterRs,
  input  [2:0] IF_ID_RegisterRt,
  output out_19,
  output out_20,
  output out_21,
  output out_22
);

  wire and_1_out, and_3_out, comparator_1_eq, comparator_2_eq, comparator_3_eq, comparator_4_eq,
       comparator_5_eq, comparator_6_eq, comparator_7_eq, comparator_8_eq, comparator_9_eq, comparator_10_eq,
       comparator_11_eq, comparator_12_eq, comparator_13_eq, not_1_out, not_2_out, not_3_out, not_4_out,
       not_5_out, not_6_out, or_1_out;

  not not_1 (not_1_out, comparator_1_eq);
  Comparator #(.width(3)) comparator_1 (.a(ID_EX_RegisterRd), .b(3'b000), .eq(comparator_1_eq));  // open: gt, lt
  and and_1 (and_1_out, ID_EX_RegWrite, not_1_out, comparator_2_eq, or_1_out);
  Comparator #(.width(3)) comparator_2 (
    .a(ID_EX_RegisterRd), .b(IF_ID_RegisterRs), .eq(comparator_2_eq));  // open: gt, lt
  or or_1 (or_1_out, BEQ, JR);
  and and_2 (out_19, EX_MEM_RegWrite, not_2_out, comparator_5_eq);
  not not_2 (not_2_out, comparator_3_eq);
  Comparator #(.width(3)) comparator_3 (.a(EX_MEM_RegisterRd), .b(3'b000), .eq(comparator_3_eq));  // open: gt, lt
  and and_3 (and_3_out, ID_EX_RegWrite, not_1_out, comparator_4_eq, BEQ);
  Comparator #(.width(3)) comparator_4 (
    .a(ID_EX_RegisterRd), .b(IF_ID_RegisterRt), .eq(comparator_4_eq));  // open: gt, lt
  Comparator #(.width(3)) comparator_5 (
    .a(EX_MEM_RegisterRd), .b(ID_EX_RegisterRs), .eq(comparator_5_eq));  // open: gt, lt
  and and_4 (out_20, EX_MEM_RegWrite, not_2_out, comparator_6_eq);
  Comparator #(.width(3)) comparator_6 (
    .a(EX_MEM_RegisterRd), .b(ID_EX_RegisterRt), .eq(comparator_6_eq));  // open: gt, lt
  // AND_Gate and_5 has open pins: in0=MEM_WB_RegWrite_2, in1=not_3_out, in2=comparator_9_eq, out=open
  not not_3 (not_3_out, comparator_7_eq);
  Comparator #(.width(3)) comparator_7 (.a(MEM_WB_RegisterRd_2), .b(3'b000), .eq(comparator_7_eq));  // open: gt, lt
  not not_4 (not_4_out, comparator_8_eq);
  Comparator #(.width(3)) comparator_8 (.a(MEM_WB_RegisterRd), .b(3'b000), .eq(comparator_8_eq));  // open: gt, lt
  Comparator #(.width(3)) comparator_9 (
    .a(MEM_WB_RegisterRd_2), .b(EX_MEM_RegisterRt), .eq(comparator_9_eq));  // open: gt, lt
  and and_6 (out_21, MEM_WB_RegWrite, not_4_out, comparator_10_eq, not_5_out);
  Comparator #(.width(3)) comparator_10 (
    .a(MEM_WB_RegisterRd), .b(ID_EX_RegisterRs_2), .eq(comparator_10_eq));  // open: gt, lt
  not not_5 (not_5_out, comparator_11_eq);
  Comparator #(.width(3)) comparator_11 (
    .a(ID_EX_RegisterRs_2), .b(EX_MEM_RegisterRd_2), .eq(comparator_11_eq));  // open: gt, lt
  and and_7 (out_22, MEM_WB_RegWrite, not_4_out, comparator_12_eq, not_6_out);
  Comparator #(.width(3)) comparator_12 (
    .a(MEM_WB_RegisterRd), .b(ID_EX_RegisterRt_2), .eq(comparator_12_eq));  // open: gt, lt
  not not_6 (not_6_out, comparator_13_eq);
  Comparator #(.width(3)) comparator_13 (
    .a(ID_EX_RegisterRt_2), .b(EX_MEM_RegisterRd_2), .eq(comparator_13_eq));  // open: gt, lt

  // Notes on the sheet:
  //   forward Rs from Alu output
  //   As the slides
  //   forward Rt from ALU output
  //   From WB into mem in case of load then store
endmodule

// Forwarding_MEM_to_EX
module MEM_to_EX (
  input  EX_MEM_RegWrite,
  input  [2:0] EX_MEM_RegisterRd,
  input  [2:0] ID_EX_RegisterRs,
  input  [2:0] ID_EX_RegisterRt,
  output MEM_to_EX_ALU1,
  output MEM_to_EX_ALU2
);

  wire comparator_1_eq, comparator_2_eq, comparator_3_eq, not_1_out;

  and and_1 (MEM_to_EX_ALU1, EX_MEM_RegWrite, not_1_out, comparator_2_eq);
  not not_1 (not_1_out, comparator_1_eq);
  Comparator #(.width(3)) comparator_1 (.a(EX_MEM_RegisterRd), .b(3'b000), .eq(comparator_1_eq));  // open: gt, lt
  Comparator #(.width(3)) comparator_2 (
    .a(EX_MEM_RegisterRd), .b(ID_EX_RegisterRs), .eq(comparator_2_eq));  // open: gt, lt
  and and_2 (MEM_to_EX_ALU2, EX_MEM_RegWrite, not_1_out, comparator_3_eq);
  Comparator #(.width(3)) comparator_3 (
    .a(EX_MEM_RegisterRd), .b(ID_EX_RegisterRt), .eq(comparator_3_eq));  // open: gt, lt
endmodule

module Forwarding_WB_to_EX (
  input  MEM_WB_RegWrite,
  input  [2:0] MEM_WB_RegisterRd,
  input  [2:0] ID_EX_RegisterRs,
  input  [2:0] ID_EX_RegisterRt,
  input  [2:0] EX_MEM_RegisterRd,
  output ALU1,
  output ALU2
);

  wire comparator_1_eq, comparator_2_eq, comparator_3_eq, comparator_4_eq, comparator_5_eq, not_1_out,
       not_2_out, not_3_out;

  not not_1 (not_1_out, comparator_1_eq);
  Comparator #(.width(3)) comparator_1 (.a(MEM_WB_RegisterRd), .b(3'b000), .eq(comparator_1_eq));  // open: gt, lt
  and and_1 (ALU1, MEM_WB_RegWrite, not_1_out, comparator_2_eq, not_2_out);
  Comparator #(.width(3)) comparator_2 (
    .a(MEM_WB_RegisterRd), .b(ID_EX_RegisterRs), .eq(comparator_2_eq));  // open: gt, lt
  not not_2 (not_2_out, comparator_3_eq);
  Comparator #(.width(3)) comparator_3 (
    .a(ID_EX_RegisterRs), .b(EX_MEM_RegisterRd), .eq(comparator_3_eq));  // open: gt, lt
  and and_2 (ALU2, MEM_WB_RegWrite, not_1_out, comparator_4_eq, not_3_out);
  Comparator #(.width(3)) comparator_4 (
    .a(MEM_WB_RegisterRd), .b(ID_EX_RegisterRt), .eq(comparator_4_eq));  // open: gt, lt
  not not_3 (not_3_out, comparator_5_eq);
  Comparator #(.width(3)) comparator_5 (
    .a(ID_EX_RegisterRt), .b(EX_MEM_RegisterRd), .eq(comparator_5_eq));  // open: gt, lt
endmodule

// F_WB_MEM
module Forwarding_WB_to_MEM (
  input  MEM_WB_RegWrite,
  input  [2:0] MEM_WB_RegisterRd,
  input  [2:0] EX_MEM_RegisterRt,
  output Store_Data
);

  wire comparator_1_eq, comparator_2_eq, not_1_out;

  and and_1 (Store_Data, MEM_WB_RegWrite, not_1_out, comparator_2_eq);
  not not_1 (not_1_out, comparator_1_eq);
  Comparator #(.width(3)) comparator_1 (.a(MEM_WB_RegisterRd), .b(3'b000), .eq(comparator_1_eq));  // open: gt, lt
  Comparator #(.width(3)) comparator_2 (
    .a(MEM_WB_RegisterRd), .b(EX_MEM_RegisterRt), .eq(comparator_2_eq));  // open: gt, lt

  // Notes on the sheet:
  //   From WB into mem in case of load then store
  //   or R-type then store
endmodule

// F_EX_ID
module Forwarding_EX_to_ID (
  input  ID_EX_RegWrite,
  input  ID_EX_MemRead,
  input  [2:0] ID_EX_RegisterRd,
  input  [2:0] IF_ID_RegisterRs,
  input  [2:0] IF_ID_RegisterRt,
  output for_RS,
  output for_RT
);

  wire comparator_1_eq, comparator_2_eq, comparator_3_eq, not_1_out, not_2_out;

  not not_1 (not_1_out, comparator_1_eq);
  Comparator #(.width(3)) comparator_1 (.a(ID_EX_RegisterRd), .b(3'b000), .eq(comparator_1_eq));  // open: gt, lt
  and and_1 (for_RS, ID_EX_RegWrite, not_1_out, not_2_out, comparator_2_eq);
  Comparator #(.width(3)) comparator_2 (
    .a(ID_EX_RegisterRd), .b(IF_ID_RegisterRs), .eq(comparator_2_eq));  // open: gt, lt
  not not_2 (not_2_out, ID_EX_MemRead);
  and and_2 (for_RT, ID_EX_RegWrite, not_1_out, not_2_out, comparator_3_eq);
  Comparator #(.width(3)) comparator_3 (
    .a(ID_EX_RegisterRd), .b(IF_ID_RegisterRt), .eq(comparator_3_eq));  // open: gt, lt

  // Notes on the sheet:
  //   forward Rs from Alu output
endmodule

// F_MEM_ID
module Forwarding_MEM_to_ID (
  input  Ex_Mem_RegWrite,
  input  [2:0] Ex_MEM_RegisterRd,
  input  [2:0] IF_ID_RegisterRs,
  input  [2:0] IF_ID_Rt_RegisterRt,
  input  EX_MEM_MemRead,
  input  [2:0] ID_EX_RegisterRd,
  output BusA,
  output BusB
);

  wire comparator_1_eq, comparator_2_eq, comparator_3_eq, comparator_4_eq, comparator_5_eq, not_1_out,
       not_2_out, not_3_out;

  not not_1 (not_1_out, comparator_1_eq);
  Comparator #(.width(3)) comparator_1 (.a(Ex_MEM_RegisterRd), .b(3'b000), .eq(comparator_1_eq));  // open: gt, lt
  and and_1 (BusA, Ex_Mem_RegWrite, not_1_out, comparator_2_eq, EX_MEM_MemRead, not_2_out);
  Comparator #(.width(3)) comparator_2 (
    .a(Ex_MEM_RegisterRd), .b(IF_ID_RegisterRs), .eq(comparator_2_eq));  // open: gt, lt
  not not_2 (not_2_out, comparator_3_eq);
  Comparator #(.width(3)) comparator_3 (
    .a(IF_ID_RegisterRs), .b(ID_EX_RegisterRd), .eq(comparator_3_eq));  // open: gt, lt
  and and_2 (BusB, Ex_Mem_RegWrite, not_1_out, comparator_4_eq, EX_MEM_MemRead, not_3_out);
  Comparator #(.width(3)) comparator_4 (
    .a(Ex_MEM_RegisterRd), .b(IF_ID_Rt_RegisterRt), .eq(comparator_4_eq));  // open: gt, lt
  not not_3 (not_3_out, comparator_5_eq);
  Comparator #(.width(3)) comparator_5 (
    .a(IF_ID_Rt_RegisterRt), .b(ID_EX_RegisterRd), .eq(comparator_5_eq));  // open: gt, lt
endmodule

module Hazard_Detection (
  input  clk,
  input  PCsrc,
  input  [23:0] PC1,
  input  [23:0] PC2,
  input  ID_EX_MemRead,
  input  [2:0] ID_EX_RegisterRd,
  input  [2:0] IF_ID_RegisterRs,
  input  IF_ID_MemWrite,
  input  [2:0] IF_ID_RegisterRt,
  output Flush_IF,
  output Flush_ID,
  output Stall_ID_Stall_IF
);

  wire and_1_out, and_5_out, comparator_1_eq, comparator_2_eq, comparator_3_eq, comparator_4_eq, d_ff_1_q,
       d_ff_2_q, not_1_out, not_2_out, not_3_out, not_4_out, or_1_out;

  not not_1 (not_1_out, comparator_1_eq);
  Comparator #(.width(24)) comparator_1 (.a(PC1), .b(PC2), .eq(comparator_1_eq));  // open: gt, lt
  and and_1 (and_1_out, PCsrc, not_1_out);
  not not_2 (not_2_out, clk);
  D_Flip_Flop #(.trigger("falling")) d_ff_1 (.clk(clk), .D(and_1_out), .Q(d_ff_1_q));  // open: Qn, preset, en, reset
  D_Flip_Flop #(.trigger("falling")) d_ff_2 (
    .clk(clk), .D(Stall_ID_Stall_IF), .Q(d_ff_2_q));  // open: Qn, preset, en, reset
  and and_2 (Stall_ID_Stall_IF, ID_EX_MemRead, not_3_out, or_1_out);
  not not_3 (not_3_out, comparator_2_eq);
  Comparator #(.width(3)) comparator_2 (.a(ID_EX_RegisterRd), .b(3'b000), .eq(comparator_2_eq));  // open: gt, lt
  Comparator #(.width(3)) comparator_3 (
    .a(ID_EX_RegisterRd), .b(IF_ID_RegisterRs), .eq(comparator_3_eq));  // open: gt, lt
  and and_3 (Flush_IF, not_2_out, d_ff_1_q);
  and and_4 (Flush_ID, clk, d_ff_2_q);
  or or_1 (or_1_out, comparator_3_eq, and_5_out);
  and and_5 (and_5_out, not_4_out, comparator_4_eq);
  not not_4 (not_4_out, IF_ID_MemWrite);
  Comparator #(.width(3)) comparator_4 (
    .a(ID_EX_RegisterRd), .b(IF_ID_RegisterRt), .eq(comparator_4_eq));  // open: gt, lt

  // Notes on the sheet:
  //   In case of missprediction
  //   In case of Load followed by a dependent instruction
endmodule

// LBU_OR_LB
module Lws_or_Lw (
  input  [23:0] mem_res,
  output [23:0] mem_final_res
);


  assign mem_final_res = mem_res;
endmodule

// F_ALURes_MEM_ID
module Forwarding_ALURes_MEM_to_ID (
  input  Ex_Mem_RegWrite,
  input  [2:0] Ex_MEM_RegisterRd,
  input  [2:0] IF_ID_RegisterRs,
  input  [2:0] IF_ID_Rt_RegisterRt,
  input  EX_MEM_MemRead,
  input  [2:0] ID_EX_RegisterRd,
  output BusA,
  output BusB
);

  wire comparator_1_eq, comparator_2_eq, comparator_3_eq, comparator_4_eq, comparator_5_eq, not_1_out,
       not_2_out, not_3_out, not_4_out;

  not not_1 (not_1_out, comparator_1_eq);
  Comparator #(.width(3)) comparator_1 (.a(Ex_MEM_RegisterRd), .b(3'b000), .eq(comparator_1_eq));  // open: gt, lt
  and and_1 (BusA, Ex_Mem_RegWrite, not_1_out, comparator_2_eq, not_2_out, not_3_out);
  not not_2 (not_2_out, EX_MEM_MemRead);
  Comparator #(.width(3)) comparator_2 (
    .a(Ex_MEM_RegisterRd), .b(IF_ID_RegisterRs), .eq(comparator_2_eq));  // open: gt, lt
  not not_3 (not_3_out, comparator_3_eq);
  Comparator #(.width(3)) comparator_3 (
    .a(IF_ID_RegisterRs), .b(ID_EX_RegisterRd), .eq(comparator_3_eq));  // open: gt, lt
  and and_2 (BusB, Ex_Mem_RegWrite, not_1_out, comparator_4_eq, not_2_out, not_4_out);
  Comparator #(.width(3)) comparator_4 (
    .a(Ex_MEM_RegisterRd), .b(IF_ID_Rt_RegisterRt), .eq(comparator_4_eq));  // open: gt, lt
  not not_4 (not_4_out, comparator_5_eq);
  Comparator #(.width(3)) comparator_5 (
    .a(IF_ID_Rt_RegisterRt), .b(ID_EX_RegisterRd), .eq(comparator_5_eq));  // open: gt, lt
endmodule
